# Fritzing sketch x y plotter arduino to processing (saved by Fritzing 0.9.3b)
breadboards: 1

parts:
  Arduino = Arduino Uno (Rev3) - ICSP
  R1 = Rotary Potentiometer (Small) [maximum_resistance=10kΩ package=THT]
  R2 = Rotary Potentiometer (Small) [maximum_resistance=10kΩ package=THT]
  C2 = Electrolytic Capacitor [capacitance=2.2µF package="100 mil [THT, electrolytic]"]
  C1 = Electrolytic Capacitor [capacitance=2.2µF package="100 mil [THT, electrolytic]"]

nets (from the breadboard view):
  N1: Arduino.A0, R2.wiper, C1.+
  N2: Arduino.A1, R1.wiper, C2.+
  N3: Arduino.5V, R1.leg2, R2.leg2
  N4: Arduino.GND, R1.leg1, R2.leg1, C2.-, C1.-

notes:
  left potentiometer
  right potentiometer
  2.2uF capacitors parallel to the potentiometer wipers to ground help stabilize the signals
